// Logisim project IC_Tester.circ as structural Verilog: 11 circuits, main circuit main
// XNOR
module main (
  input  Not_Working,
  input  Reset,
  input  Enable,
  output Not_Found,
  output Found,
  output [1:0] \output 
);

  wire _1, _2, _3, _4, and_4_out, C1, C2, Clock, Enabling_the_project, F, input_1, input_2, is_4,
       One_gate_output, Reset_t, tunnel, xor_1_out;
  wire [3:1] AND_3_gate_b;

  Clock u_Clock (.out(Clock));
  and and_1 (Reset_t, Enable, Reset);
  Counter Counter (
    .Clock(Clock), .Enable(Enabling_the_project), .Reset(Reset_t), .out_4(input_1), .out_5(input_2),
    .out_6(is_4));
  Shift_Register shift_register_1 (
    .Clock(Clock), .Enable(Enabling_the_project), .Reset(Reset_t), .Input(One_gate_output), .most_right(_1),
    .out_6(_2), .out_7(_3), .most_left(_4));
  XNOR XNOR ();  // open: in_1, in_2, Not_Working_if___1, Gate_a, Gate_b, Gate_c, Gate_d
  AND AND_2 ();  // open: in_1, in_2, Not_Working_if___1, Gate_a, Gate_b, Gate_c, Gate_d
  xor xor_1 (xor_1_out, 1'b1, is_4);
  Compare Compare (.A(_1), .B(_2), .C(_3), .D(_4), .C1(C1), .C2(C2), .F(F));
  XOR XOR_2 ();  // open: in_1, in_2, Not_Working_if___1, Gate_a, Gate_b, Gate_c, Gate_d
  OR OR ();  // open: in_1, in_2, Not_Working_if___1, Gate_a, Gate_b, Gate_c, Gate_d
  AND AND_3 (
    .in_1(input_1), .in_2(input_2), .Not_Working_if___1(Not_Working), .Gate_a(One_gate_output),
    .Gate_b(AND_3_gate_b[1]), .Gate_c(AND_3_gate_b[2]), .Gate_d(AND_3_gate_b[3]));
  and and_4 (and_4_out, xor_1_out, Enable);
  NAND NAND ();  // open: in_1, in_2, Not_Working_if___1, Gate_a, Gate_b, Gate_c, Gate_d
  All_equal All_equal (.in_1({AND_3_gate_b, One_gate_output}), .out_2(tunnel));
  and and_5 (Enabling_the_project, tunnel, and_4_out);
  Result result_1 (
    .in_1(tunnel), .Found(F), .is_4(is_4), .C1_in(C1), .C2_in(C2), .Not_Found(Not_Found), .Found_2(Found),
    .C1(\output [0]), .C2(\output [1]));

  // Notes on the sheet:
  //   Shift REG
  //   Result
endmodule

module Counter (
  input  Clock,
  input  Enable,
  input  Reset,
  output out_4,
  output out_5,
  output out_6
);

  wire AB;

  T_Flip_Flop Counter_1_a (.clk(Clock), .T(1'b1), .Q(out_4), .preset(1'b0), .reset(Reset), .en(Enable));  // open: Qn
  T_Flip_Flop Counter_1_b (.clk(Clock), .T(out_4), .Q(out_5), .preset(1'b0), .reset(Reset), .en(Enable));  // open: Qn
  T_Flip_Flop Counter_1_c (.clk(Clock), .T(AB), .Q(out_6), .preset(1'b0), .reset(Reset), .en(Enable));  // open: Qn
  and and_1 (AB, out_4, out_5);

  // Other names for the same wires on the sheet: a = out_4; b = out_5
endmodule

module Shift_Register (
  input  Clock,
  input  Enable,
  input  Reset,
  input  Input,
  output most_right,
  output out_6,
  output out_7,
  output most_left
);

  Shift_Register_part #(.length(4)) shift_register_1 (
    .shift(Enable), .in(Input), .clk(Clock), .clr(Reset), .q0(most_left), .q1(out_7), .q2(out_6),
    .q3(most_right));  // open: out, load, d0, d1, d2, d3
endmodule

module All_equal (
  input  [3:0] in_1,
  output out_2
);

  wire multiplexer_1_out;
  wire [1:0] xor_1_out;

  Multiplexer #(.select(2), .enable("false")) multiplexer_1 (
    .in0(1'b1), .in1(1'b0), .in2(1'b0), .in3(1'b1), .out(multiplexer_1_out), .sel(in_1[3:2]));
  xor xor_1 (xor_1_out[0], in_1[2], in_1[1]);
  xor xor_2 (xor_1_out[1], in_1[1], in_1[0]);
  Multiplexer #(.select(2), .enable("false")) multiplexer_2 (
    .in0(multiplexer_1_out), .in1(1'b0), .in2(1'b0), .in3(1'b0), .out(out_2), .sel(xor_1_out));
endmodule

module Compare (
  input  A,
  input  B,
  input  C,
  input  D,
  output C1,
  output C2,
  output F
);

  wire and_2_out, and_3_out, and_4_out, BC, not_1_out, not_2_out, not_3_out, not_4_out, or_1_out, xor_1_out;

  not not_1 (not_1_out, A);
  not not_2 (not_2_out, B);
  not not_3 (not_3_out, C);
  not not_4 (not_4_out, D);
  and and_1 (BC, B, C);
  xor xor_1 (xor_1_out, A, D);
  or or_1 (or_1_out, C1, C2);
  and and_2 (and_2_out, not_1_out, not_2_out);
  and and_3 (and_3_out, and_2_out, and_4_out);
  and and_4 (and_4_out, D, not_3_out);
  and and_5 (C1, BC, xor_1_out);
  and and_6 (C2, BC, not_4_out);
  or or_2 (F, or_1_out, and_3_out);
endmodule

module Result (
  input  in_1,
  input  Found,
  input  is_4,
  input  C1_in,
  input  C2_in,
  output Not_Found,
  output Found_2,
  output C1,
  output C2
);

  wire and_1_out, not_1_out, not_2_out;

  not not_1 (not_1_out, Found_2);
  not not_2 (not_2_out, in_1);
  and and_1 (and_1_out, is_4, not_1_out);
  and and_2 (Found_2, Found, is_4);
  and and_3 (C1, Found_2, C1_in);
  and and_4 (C2, Found_2, C2_in);
  or or_1 (Not_Found, and_1_out, not_2_out);

  // Other names for the same wires on the sheet: Found_t = Found_2
endmodule

module OR (
  input  in_1,
  input  in_2,
  input  Not_Working_if___1,
  output Gate_a,
  output Gate_b,
  output Gate_c,
  output Gate_d
);

  wire not_1_out, or_4_out;

  or or_1 (Gate_a, in_1, in_2);
  or or_2 (Gate_b, in_1, in_2);
  or or_3 (Gate_c, in_1, in_2);
  or or_4 (or_4_out, in_1, in_2);
  not not_1 (not_1_out, or_4_out);
  Multiplexer #(.enable("false")) multiplexer_1 (
    .in0(or_4_out), .in1(not_1_out), .out(Gate_d), .sel(Not_Working_if___1));
endmodule

module AND (
  input  in_1,
  input  in_2,
  input  Not_Working_if___1,
  output Gate_a,
  output Gate_b,
  output Gate_c,
  output Gate_d
);

  wire and_4_out, not_1_out;

  and and_1 (Gate_a, in_1, in_2);
  and and_2 (Gate_b, in_1, in_2);
  and and_3 (Gate_c, in_1, in_2);
  and and_4 (and_4_out, in_1, in_2);
  not not_1 (not_1_out, and_4_out);
  Multiplexer #(.enable("false")) multiplexer_1 (
    .in0(and_4_out), .in1(not_1_out), .out(Gate_d), .sel(Not_Working_if___1));
endmodule

module NAND (
  input  in_1,
  input  in_2,
  input  Not_Working_if___1,
  output Gate_a,
  output Gate_b,
  output Gate_c,
  output Gate_d
);

  wire nand_4_out, not_1_out;

  nand nand_1 (Gate_a, in_1, in_2);
  nand nand_2 (Gate_b, in_1, in_2);
  nand nand_3 (Gate_c, in_1, in_2);
  nand nand_4 (nand_4_out, in_1, in_2);
  not not_1 (not_1_out, nand_4_out);
  Multiplexer #(.enable("false")) multiplexer_1 (
    .in0(nand_4_out), .in1(not_1_out), .out(Gate_d), .sel(Not_Working_if___1));
endmodule

module XOR (
  input  in_1,
  input  in_2,
  input  Not_Working_if___1,
  output Gate_a,
  output Gate_b,
  output Gate_c,
  output Gate_d
);

  wire not_1_out, xor_4_out;

  xor xor_1 (Gate_a, in_1, in_2);
  xor xor_2 (Gate_b, in_1, in_2);
  xor xor_3 (Gate_c, in_1, in_2);
  xor xor_4 (xor_4_out, in_1, in_2);
  not not_1 (not_1_out, xor_4_out);
  Multiplexer #(.enable("false")) multiplexer_1 (
    .in0(xor_4_out), .in1(not_1_out), .out(Gate_d), .sel(Not_Working_if___1));
endmodule

module XNOR (
  input  in_1,
  input  in_2,
  input  Not_Working_if___1,
  output Gate_a,
  output Gate_b,
  output Gate_c,
  output Gate_d
);

  wire not_1_out, xnor_4_out;

  xnor xnor_1 (Gate_a, in_1, in_2);
  xnor xnor_2 (Gate_b, in_1, in_2);
  xnor xnor_3 (Gate_c, in_1, in_2);
  xnor xnor_4 (xnor_4_out, in_1, in_2);
  Multiplexer #(.enable("false")) multiplexer_1 (
    .in0(xnor_4_out), .in1(not_1_out), .out(Gate_d), .sel(Not_Working_if___1));
  not not_1 (not_1_out, xnor_4_out);
endmodule
